# Fritzing sketch schemat (saved by Fritzing 0.9.3b)
breadboards: 3

parts:
  Part1 = Arduino Leonardo (Rev3b)
  U1 = PCF8574 [package="DIP16 [THT]"]
  U2 = PCF8574 [package="DIP16 [THT]"]
  LED1 = LED - 3mm [color="Red (633nm)" package="3 mm [THT]"]
  LED2 = LED - 3mm [color="Yellow (595nm)" package="3 mm [THT]"]
  LED3 = LED - 3mm [color="Green (570nm)" package="3 mm [THT]"]
  R1 = Resistor [tolerance=±5% resistance=220 package=THT]
  R2 = Resistor [tolerance=±5% resistance=220 package=THT]
  R3 = Resistor [tolerance=±5% resistance=220 package=THT]
  LED4 = LED - 3mm [color="Yellow (595nm)" package="3 mm [THT]"]
  LED5 = LED - 3mm [color="Green (570nm)" package="3 mm [THT]"]
  LED6 = LED - 3mm [color="Red (633nm)" package="3 mm [THT]"]
  R4 = Resistor [tolerance=±5% resistance=220 package=THT]
  R5 = Resistor [tolerance=±5% resistance=220 package=THT]
  R6 = Resistor [tolerance=±5% resistance=220 package=THT]
  LED7 = LED - 3mm [color="Yellow (595nm)" package="3 mm [THT]"]
  LED8 = LED - 3mm [color="Green (570nm)" package="3 mm [THT]"]
  LED9 = LED - 3mm [color="Red (633nm)" package="3 mm [THT]"]
  R7 = Resistor [tolerance=±5% resistance=220 package=THT]
  R8 = Resistor [tolerance=±5% resistance=220 package=THT]
  R9 = Resistor [tolerance=±5% resistance=220 package=THT]
  LED10 = LED - 3mm [color="Yellow (595nm)" package="3 mm [THT]"]
  LED11 = LED - 3mm [color="Green (570nm)" package="3 mm [THT]"]
  LED12 = LED - 3mm [color="Red (633nm)" package="3 mm [THT]"]
  R10 = Resistor [tolerance=±5% resistance=220 package=THT]
  R11 = Resistor [tolerance=±5% resistance=220 package=THT]
  R12 = Resistor [tolerance=±5% resistance=220 package=THT]
  S1 = Pushbutton [package="[SMD]"]
  S2 = Pushbutton [package="[SMD]"]
  R13 = Resistor [tolerance=±5% resistance=220 package=THT]
  R14 = Resistor [tolerance=±5% resistance=220 package=THT]

nets:
  N1: Part1.D6_PWM/A7, S2.Pin_1, S2.Pin_2, R14.Pin_1
  N2: Part1.D7, S1.Pin_1, S1.Pin_2, R13.Pin_1
  VCC: Part1.5V, U1.A3, U1.VCC, U2.VCC, S1.Pin_3, S1.Pin_4, S2.Pin_3, S2.Pin_4
  GND: Part1.GND, U1.A0, U1.A1, U1.GND, U2.A0, U2.A1, U2.A3, U2.GND, R13.Pin_0, R14.Pin_0
  N3: Part1.SDA, U1.SDA, U2.SDA
  N4: Part1.SCL, U1.SCL, U2.SCL
  N5: U1.P0, R1.Pin_1
  N6: U1.P1, R2.Pin_1
  N7: U1.P2, R3.Pin_1
  N8: U1.P3, R5.Pin_1
  N9: U1.P4, R4.Pin_1, R6.Pin_1
  N10: U2.P0, R8.Pin_1
  N11: U2.P1, R7.Pin_1
  N12: U2.P2, R9.Pin_1
  N13: U2.P3, R11.Pin_1
  N14: U2.P4, R10.Pin_1
  N15: U2.P5, R12.Pin_1
  N16: LED1.cathode, LED2.cathode, LED3.cathode, LED4.cathode, LED5.cathode, LED6.cathode, LED7.cathode, LED8.cathode, LED9.cathode, LED10.cathode, LED11.cathode, LED12.cathode
  N17: LED1.anode, R1.Pin_0
  N18: LED2.anode, R2.Pin_0
  N19: LED3.anode, R3.Pin_0
  N20: LED4.anode, R4.Pin_0
  N21: LED5.anode, R6.Pin_0
  N22: LED6.anode, R5.Pin_0
  N23: LED7.anode, R7.Pin_0
  N24: LED8.anode, R9.Pin_0
  N25: LED9.anode, R8.Pin_0
  N26: LED10.anode, R10.Pin_0
  N27: LED11.anode, R12.Pin_0
  N28: LED12.anode, R11.Pin_0

// code stored in the sketch: Untitled2.ino
//deklaracja bibliotek
#include <PortExpander_I2C.h>
#include <Wire.h>

//definicja pinow czujnika odleglosci
#define trigPin 12
#define echoPin 11

//definicja ekspanderów
PortExpander_I2C pe1(0x20);
PortExpander_I2C pe2(0x24);

//deklaracja zmienniej true / false: tryb 2
boolean zm = false;

//deklaracja trybów
int tryb = 1;

//deklaracja guzikow
int ztryb = 6; //zmiana trybu
int zswiatla = 7; //zmiana swiatel w trybie 2

//deklaracja diod
//swiatla 1
int czerwony1 = 0;
int pomaranczowu1 = 1;
int zielony1 = 2;

//swiatla 2
int czerwony2 = 3;
int pomaranczowu2 = 4;
int zielony2 = 5;

//swiatla 3
int czerwony3 = 0;
int pomaranczowu3 = 1;
int zielony3 = 2;

//swiatla 4
int czerwony4 = 3;
int pomaranczowu4 = 4;
int zielony4 = 5;

void setup() {
  //deklaracja czujnika1
  pinMode(trigPin, OUTPUT);
  pinMode(echoPin, INPUT);

  //deklaracja guzikow
  pinMode (INPUT, zswiatla);
  pinMode(INPUT, ztryb);

  //uruchomienie ekspanderow
  pe1.init();
  pe2.init();

  //swiatla 1
  pe1.pinMode(OUTPUT, czerwony1);
  pe1.pinMode(OUTPUT, pomaranczowu1);
  pe1.pinMode(OUTPUT, zielony1);

  //swiatla 2
  pe1.pinMode(OUTPUT, czerwony2);
  pe1.pinMode(OUTPUT, pomaranczowu2);
  pe1.pinMode(OUTPUT, zielony2);

  //swiatla 3
  pe2.pinMode(OUTPUT, czerwony3);
  pe2.pinMode(OUTPUT, pomaranczowu3);
  pe2.pinMode(OUTPUT, zielony3);

  //swiatla 4
  pe2.pinMode(OUTPUT, czerwony4);
  pe2.pinMode(OUTPUT, pomaranczowu4);
  pe2.pinMode(OUTPUT, zielony4);
}

//funkcja czujnika1
int zmierzOdleglosc() {
  long czas, dystans;

  digitalWrite(trigPin, LOW);
  delayMicroseconds(2);
  digitalWrite(trigPin, HIGH);
  delayMicroseconds(10);
  digitalWrite(trigPin, LOW);

  czas = pulseIn(echoPin, HIGH);
  dystans = czas / 58;

  return dystans;
}
//funkcja zamiany swiatel
void cz1() {
  pe1.digitalWrite(pomaranczowu1, HIGH);
  pe2.digitalWrite(pomaranczowu3, HIGH);
  delay(1000);
  pe2.digitalWrite(czerwony3, LOW);
  pe1. digitalWrite(czerwony1, LOW);
  pe1.digitalWrite(pomaranczowu1, LOW);
  pe2.digitalWrite(pomaranczowu3, LOW);
  pe2.digitalWrite(zielony3, HIGH);
  pe1.digitalWrite(zielony1, HIGH);
}

void zc1() {
  pe2.digitalWrite(zielony3, LOW);
  pe1.digitalWrite(zielony1, LOW);
  pe1.digitalWrite(pomaranczowu1, HIGH);
  pe2.digitalWrite(pomaranczowu3, HIGH);
  delay(1000);
  pe1.digitalWrite(pomaranczowu1, LOW);
  pe2.digitalWrite(pomaranczowu3, LOW);
  pe2.digitalWrite(czerwony3, HIGH);
  pe1. digitalWrite(czerwony1, HIGH);
}

void cz2() {
  pe1.digitalWrite(pomaranczowu2, HIGH);
  pe2.digitalWrite(pomaranczowu4, HIGH);
  delay(1000);
  pe2.digitalWrite(czerwony2, LOW);
  pe1. digitalWrite(czerwony4, LOW);
  pe1.digitalWrite(pomaranczowu2, LOW);
  pe2.digitalWrite(pomaranczowu4, LOW);
  pe2.digitalWrite(zielony2, HIGH);
  pe1.digitalWrite(zielony4, HIGH);
}
void zc2() {
  pe2.digitalWrite(zielony2, LOW);
  pe1.digitalWrite(zielony4, LOW);
  pe1.digitalWrite(pomaranczowu2, HIGH);
  pe2.digitalWrite(pomaranczowu4, HIGH);
  delay(1000);
  pe1.digitalWrite(pomaranczowu2, LOW);
  pe2.digitalWrite(pomaranczowu4, LOW);
  pe2.digitalWrite(czerwony2, HIGH);
  pe1. digitalWrite(czerwony4, HIGH);

}
//dodawanie do trybu (tryb++)
void trybplus() {

  if (digitalRead(ztryb) == HIGH) {
    delay(500);
    tryb++;
    Serial.println(tryb);
  }
  while (digitalRead(ztryb) == HIGH);
  if (tryb > 4) {
    tryb = 1;
  }
}

//tryb awaryjny
void awaryjne() {
  pe1.digitalWrite(zielony1, LOW);
  pe1.digitalWrite(zielony2, LOW);
  pe2.digitalWrite(zielony3, LOW);
  pe2.digitalWrite(zielony4, LOW);
  pe1.digitalWrite(czerwony1, LOW);
  pe1.digitalWrite(czerwony2, LOW);
  pe2.digitalWrite(czerwony3, LOW);
  pe2.digitalWrite(czerwony4, LOW);


  pe1.digitalWrite(pomaranczowu1, HIGH);
  pe1.digitalWrite(pomaranczowu2, HIGH);
  pe2.digitalWrite(pomaranczowu3, HIGH);
  pe2.digitalWrite(pomaranczowu4, HIGH);
  delay(1500);
  pe1.digitalWrite(pomaranczowu1, LOW);
  pe1.digitalWrite(pomaranczowu2, LOW);
  pe2.digitalWrite(pomaranczowu3, LOW);
  pe2.digitalWrite(pomaranczowu4, LOW);
  delay(1500);
}

void loop() {

  trybplus();
  if (tryb == 1) {
    trybplus();
    delay(2000);
    trybplus();
    zc2();
    trybplus();
    cz1();
    trybplus();
    delay(2000);
    trybplus();
    zc1();
    trybplus();
    cz2();
  } else  if (tryb == 2) {
    if (digitalRead(zswiatla) == HIGH) {
      delay(50);
      zm = !zm;
      if (zm == true) {
        zc2();
        cz1();
      } else {
        zc1();
        cz2();
      }
    }
  } else if (tryb == 3) {
    pe1.digitalWrite(zielony2, LOW);
    pe2.digitalWrite(zielony4, LOW);
    if (zmierzOdleglosc() < 30) {
      pe1.digitalWrite(pomaranczowu1, HIGH);
      pe2.digitalWrite(pomaranczowu3, HIGH);
      delay(1000);
      pe1.digitalWrite(czerwony1, LOW);
      pe2.digitalWrite(czerwony3, LOW);
      pe1.digitalWrite(pomaranczowu1, LOW);
      pe2.digitalWrite(pomaranczowu3, LOW);
      pe1.digitalWrite(zielony1, HIGH);
      pe2.digitalWrite(zielony3, HIGH);
      delay(5000);
      pe1.digitalWrite(zielony1, LOW);
      pe2.digitalWrite(zielony3, LOW);
      pe1.digitalWrite(pomaranczowu1, HIGH);
      pe2.digitalWrite(pomaranczowu3, HIGH);
      delay(1000);
      pe1.digitalWrite(pomaranczowu1, LOW);
      pe2.digitalWrite(pomaranczowu3, LOW);
    } else {
      pe1.digitalWrite(czerwony2, HIGH);
      pe2.digitalWrite(czerwony4, HIGH);
      pe1.digitalWrite(czerwony1, HIGH);
      pe2.digitalWrite(czerwony3, HIGH);
    }
  } else if (tryb == 4) {
    awaryjne();
  }

}
